# Fritzing sketch Schematic_Wifi_weather_station_r00_22092019 (saved by Fritzing 0.9.2b)

parts:
  U1 = ESP8266-12 WiFi Module [part_number=ESP8266]
  R1 = Resistor [tolerance=±5% resistance=10k package="0603 [SMD]"]
  R2 = Resistor [tolerance=±5% resistance=10k package="0603 [SMD]"]
  R3 = Resistor [tolerance=±5% resistance=10k package="0603 [SMD]"]
  R4 = Resistor [tolerance=±5% resistance=10k package="0603 [SMD]"]
  Componente1 = FTDI Basic Programmer
  S1 = Momentary Switch [package=ksa_sealed_tac_switch]
  R5 = Resistor [tolerance=±5% resistance=1k package="0603 [SMD]"]
  LED1 = LED - 3mm [color="Red (633nm)" package="3 mm [THT]"]
  C1 = Capacitor [package=cap-pth-small2]  # not connected

nets:
  N1: U1.GPIO_0, R2.Pin_0
  N2: U1.CH_PD, R4.Pin_1
  GND: U1.GND, Componente1.GND
  N3: U1.TXD, Componente1.RXI
  N4: U1.GPIO_12, R5.Pin_1
  N5: U1.GPIO_15, R3.Pin_0
  N6: U1.RESET, R1.Pin_1, S1.1
  N7: U1.RXD, Componente1.TXO
  N8: U1.VCC, R2.Pin_1
  N9: R5.Pin_0, LED1.anode

notes:
  Reset
  GPIO12
  TX
  RX
  GND
  +3.3V
  CH_PD
  GPIO15
  GPIO0
  Jumper
  Fechar para
  Programar o ESP12
  ADC
  GPIO16
  GPIO14
  GPIO13
  GPIO2
  GPIO5
  GPIO4
  10k ohm
  1k ohm
  ESP-12
  Qualquer modelo
  de conversor Serial
  100 nF

custom parts:
  ESP8266-12 WiFi Module: Generic WiFi Module based on the ESP8266 with onboard PCB antenna and UART communications
